# Fritzing sketch IoT_RemoteControl_Circuit (saved by Fritzing 0.9.3b)
breadboards: 1

parts:
  LED1 = LED - 5mm [color="Red (633nm)" package="5 mm [THT]"]
  2N3904 = NPN-Transistor [package="TO92 [THT]"]
  CHQ1838D = TSOP312.., 314.. [package=THT]
  U1 = NodeMCU V1.0

nets:
  N1: LED1.cathode, 2N3904.C
  N2: LED1.anode, CHQ1838D.Data, U1.3V3
  N3: 2N3904.E, CHQ1838D.Vs, U1.GND
  N4: 2N3904.B, U1.D2
  N5: CHQ1838D.GND, U1.D5

notes:
  IR Receiver: CHQ1838D
  Triode: 2N3904
  NodeMCU: ESP12-E

custom parts:
  NodeMCU V1.0: ESP8266 based NodeMCU
